# Fritzing sketch 01_dual_color_led (saved by Fritzing 0.8.7b)
breadboards: 1

parts:
  T-Cobbler1 = T-Cobbler
  module2 = Dule-Color LED

nets:
  N1: T-Cobbler1.GPIO17, module2.R
  N2: T-Cobbler1.GND#22, module2.GND
  N3: T-Cobbler1.GPIO18, module2.G

notes:
  Dual_Color LED

custom parts:
  T-Cobbler: T-Cobbler for RPi B+ and Rpi2 from SunFounder
  Dule-Color LED: DuleColor LED module of SunFounder Sensor Kit
