# Fritzing sketch 02_RGB_LED (saved by Fritzing 0.9.2b)
breadboards: 1

parts:
  T-Cobbler1 = T-Cobbler
  module1 = RGB LED

nets:
  N1: T-Cobbler1.GPIO17, module1.R
  N2: T-Cobbler1.GPIO27, module1.B
  N3: T-Cobbler1.5V0#20, module1.VCC
  N4: T-Cobbler1.GPIO18, module1.G

notes:
  RGB LED

custom parts:
  T-Cobbler: T-Cobbler for RPi B+ and Rpi2 from SunFounder
  RGB LED: RGB LED module of SunFounder Sensor Kit
