# Fritzing sketch 03_AutoFlashLED (saved by Fritzing 0.9.3b)
breadboards: 1

parts:
  T-Cobbler1 = T-Cobbler
  module2 = AutoFlashLED

nets:
  N1: T-Cobbler1.3V3#0, module2.VCC
  N2: T-Cobbler1.GND#4, module2.GND#6

notes:
  Auto-flash LED

custom parts:
  T-Cobbler: T-Cobbler for RPi B+ and Rpi2 from SunFounder
  AutoFlashLED: Auto Flash LED module of SunFounder Sensor Kit
