# Fritzing sketch 05_Laser (saved by Fritzing 0.9.2b)
breadboards: 1

parts:
  T-Cobbler1 = T-Cobbler
  module3 = Laser

nets:
  N1: T-Cobbler1.GPIO17, module3.SIG
  N2: T-Cobbler1.5V0#20, module3.VCC

notes:
  Laser

custom parts:
  T-Cobbler: T-Cobbler for RPi B+ and Rpi2 from SunFounder
  Laser: Laser module for SunFounder Sensor Kit
