# Fritzing sketch 07_Tilt-Switch (saved by Fritzing 0.9.3b)
breadboards: 1

parts:
  T-Cobbler1 = T-Cobbler
  module5 = Dule-Color LED
  module7 = Tilt Switch

nets:
  N1: T-Cobbler1.3V3#0, module7.VCC
  N2: T-Cobbler1.GND#4, module7.GND
  N3: T-Cobbler1.GPIO17, module7.SIG
  N4: T-Cobbler1.GPIO27, module5.G
  N5: T-Cobbler1.GPIO18, module5.R
  N6: T-Cobbler1.GND#36, module5.GND

notes:
  Tilt Switch
  Dual-color LED

custom parts:
  T-Cobbler: T-Cobbler for RPi B+ and Rpi2 from SunFounder
  Dule-Color LED: DuleColor LED module of SunFounder Sensor Kit
