# Fritzing sketch 09_IR Receiver.svg (saved by Fritzing 0.9.2b)
breadboards: 1

parts:
  T-Cobbler1 = T-Cobbler
  module8 = IR Receiver

nets:
  N1: T-Cobbler1.GPIO17, module8.SIG
  N2: T-Cobbler1.5V0#20, module8.VCC
  N3: T-Cobbler1.GND#22, module8.GND

notes:
  IR Receiver

custom parts:
  T-Cobbler: T-Cobbler for RPi B+ and Rpi2 from SunFounder
  IR Receiver: IR Receiver module of SunFounder Sensor Kit
