# Fritzing sketch 10_Passive Buzzer (saved by Fritzing 0.9.2b)
breadboards: 1

parts:
  T-Cobbler1 = T-Cobbler
  module9 = Buzzer

nets:
  N1: T-Cobbler1.GPIO17, module9.SIG
  N2: T-Cobbler1.5V0#20, module9.VCC
  N3: T-Cobbler1.GND#22, module9.GND

notes:
  Passive Buzzer

custom parts:
  T-Cobbler: T-Cobbler for RPi B+ and Rpi2 from SunFounder
  Buzzer: Buzzer module of SunFounder Sensor Kit
