# Fritzing sketch 11_Reed switch (saved by Fritzing 0.9.3b)
breadboards: 1

parts:
  T-Cobbler1 = T-Cobbler
  module5 = Dule-Color LED
  module10 = Reed Switch

nets:
  N1: T-Cobbler1.GND#4, module10.GND
  N2: T-Cobbler1.GPIO17, module10.SIG
  N3: T-Cobbler1.GPIO27, module5.G
  N4: T-Cobbler1.3V3#8, module10.VCC
  N5: T-Cobbler1.GND#12, module5.GND
  N6: T-Cobbler1.GPIO18, module5.R

notes:
  Reed Switch
  Dual-color LED

custom parts:
  T-Cobbler: T-Cobbler for RPi B+ and Rpi2 from SunFounder
  Dule-Color LED: DuleColor LED module of SunFounder Sensor Kit
  Reed Switch: Reed Switch module of SunFounder Sensor Kit
