# Fritzing sketch 14_Rain Detection (saved by Fritzing 0.9.3b)
breadboards: 1

parts:
  T-Cobbler1 = T-Cobbler
  module10 = PCF8591
  module11 = Rain Detection board
  module12 = LM393

nets:
  N1: T-Cobbler1.3V3#0, module10.VCC
  N2: T-Cobbler1.SDA1, module10.SDA
  N3: T-Cobbler1.SCL1, module10.SCL
  N4: T-Cobbler1.GND#4, module10.GND
  N5: T-Cobbler1.GPIO17, module12.DO
  N6: T-Cobbler1.3V3#8, module12.VCC
  N7: T-Cobbler1.GND#12, module12.GND#8
  N8: module10.AIN0, module12.AO
  N9: module11.+, module12.GND#10
  N10: module11.-, module12.IN

notes:
  PCF8591
  Rain detection

custom parts:
  T-Cobbler: T-Cobbler for RPi B+ and Rpi2 from SunFounder
  PCF8591: PCF8591 ADC module for SunFounder Sensor Kit
  Rain Detection board: Rain Detection board for SunFounder Sensor Kit (along with LM393).
  LM393: LM393 module of SunFounder Sensor Kit
