# Fritzing sketch 15_JoyStick_PS2 (saved by Fritzing 0.9.3b)
breadboards: 1

parts:
  T-Cobbler1 = T-Cobbler
  module10 = PCF8591
  module13 = JoyStick

nets:
  N1: T-Cobbler1.3V3#0, module10.VCC
  N2: T-Cobbler1.SDA1, module10.SDA
  N3: T-Cobbler1.SCL1, module10.SCL
  N4: T-Cobbler1.GND#4, module10.GND
  N5: T-Cobbler1.3V3#8, module13.VCC
  N6: T-Cobbler1.GND#12, module13.GND
  N7: module10.AIN1, module13.X
  N8: module10.AIN2, module13.BT
  N9: module10.AIN0, module13.Y

notes:
  PCF8591
  Joystick

custom parts:
  T-Cobbler: T-Cobbler for RPi B+ and Rpi2 from SunFounder
  PCF8591: PCF8591 ADC module for SunFounder Sensor Kit
  JoyStick: JoyStick module of SunFounder Sensor Kit
