# Fritzing sketch 22_Gas Sensor (saved by Fritzing 0.9.2b)
breadboards: 1

parts:
  T-Cobbler1 = T-Cobbler
  module10 = PCF8591
  module21 = MQ-2 Gas Sensor
  module22 = Buzzer

nets:
  N1: T-Cobbler1.3V3#0, module10.VCC
  N2: T-Cobbler1.SDA1, module10.SDA
  N3: T-Cobbler1.SCL1, module10.SCL
  N4: T-Cobbler1.GPIO17, module21.DO
  VCC: T-Cobbler1.5V0#20, module21.VCC, module22.VCC
  GND: T-Cobbler1.GND#22, module10.GND, module21.GND, module22.GND
  N5: T-Cobbler1.GPIO18, module22.SIG
  N6: module10.AIN0, module21.AO

notes:
  PCF8591
  Gas Sensor
  Active Buzzer

custom parts:
  T-Cobbler: T-Cobbler for RPi B+ and Rpi2 from SunFounder
  PCF8591: PCF8591 ADC module for SunFounder Sensor Kit
  MQ-2 Gas Sensor: MQ-2 Gas Sensor module of SunFounder Sensor Kit
  Buzzer: Buzzer module of SunFounder Sensor Kit
