# Fritzing sketch 23_IR remote control (saved by Fritzing 0.9.3b)
breadboards: 1

parts:
  T-Cobbler1 = T-Cobbler
  module8 = IR Receiver
  module9 = RGB LED

nets:
  N1: T-Cobbler1.3V3#0, module8.VCC
  N2: T-Cobbler1.GND#4, module8.GND
  N3: T-Cobbler1.GPIO17, module9.R
  N4: T-Cobbler1.GPIO27, module9.B
  N5: T-Cobbler1.3V3#8, module9.VCC
  N6: T-Cobbler1.GPIO18, module9.G
  N7: T-Cobbler1.GPIO23, module8.SIG

notes:
  IR Receiver
  RGB LED

custom parts:
  T-Cobbler: T-Cobbler for RPi B+ and Rpi2 from SunFounder
  IR Receiver: IR Receiver module of SunFounder Sensor Kit
  RGB LED: RGB LED module of SunFounder Sensor Kit
