# Fritzing sketch 25_Ultrasonic_Ranging (saved by Fritzing 0.9.3b)
breadboards: 1

parts:
  T-Cobbler1 = T-Cobbler
  module4 = Ultrasonic-HC-SRO4

nets:
  N1: T-Cobbler1.3V3#0, module4.VCC
  N2: T-Cobbler1.GPIO17, module4.TRIG
  N3: T-Cobbler1.GND#12, module4.GND
  N4: T-Cobbler1.GPIO18, module4.ECHO

custom parts:
  T-Cobbler: T-Cobbler for RPi B+ and Rpi2 from SunFounder
  Ultrasonic-HC-SRO4: The ultrasonic sensor uses sound to accurately detect objects and measure distances. It sends out ultrasonic waves and converts them into electronic signals
