# Fritzing sketch 26_DS18B20 (saved by Fritzing 0.9.2b)
breadboards: 1

parts:
  T-Cobbler1 = T-Cobbler
  module1 = DS18B20 module

nets:
  N1: T-Cobbler1.GPIO4, module1.SIG
  N2: T-Cobbler1.5V0#20, module1.VCC
  N3: T-Cobbler1.GND#22, module1.GND

notes:
  DS18B20

custom parts:
  T-Cobbler: T-Cobbler for RPi B+ and Rpi2 from SunFounder
  DS18B20 module: DS18B20 module from SunFounder Sensor Kit
