# Fritzing sketch 27_Rotary Encode (saved by Fritzing 0.9.3b)
breadboards: 1

parts:
  T-Cobbler1 = T-Cobbler
  module2 = Rotary Encoder

nets:
  N1: T-Cobbler1.GPIO17, module2.CLK
  N2: T-Cobbler1.GPIO27, module2.SW
  N3: T-Cobbler1.3V3#8, module2.VCC
  N4: T-Cobbler1.GND#12, module2.GND
  N5: T-Cobbler1.GPIO18, module2.DT

notes:
  Rotary Encoder

custom parts:
  T-Cobbler: T-Cobbler for RPi B+ and Rpi2 from SunFounder
  Rotary Encoder: Rotary Encoder module of SunFounder Sensor Kit
