# Fritzing sketch 30_I2C LCD1602 (saved by Fritzing 0.9.3b)
breadboards: 1

parts:
  T-Cobbler1 = T-Cobbler
  module5 = I2C LCD1602

nets:
  N1: T-Cobbler1.SDA1, module5.SDA
  N2: T-Cobbler1.SCL1, module5.SCL
  N3: T-Cobbler1.5V0#20, module5.VCC
  N4: T-Cobbler1.GND#22, module5.GND

notes:
  I2C LCD1602

custom parts:
  T-Cobbler: T-Cobbler for RPi B+ and Rpi2 from SunFounder
  I2C LCD1602: I2C LCD1602 module of SunFounder Sensor Kit
