# Fritzing sketch 31_BMP280 (saved by Fritzing 0.8.7b)
breadboards: 1

parts:
  U1 = BMP280 Module [package="DIP7 [THT]"]
  T-Cobbler1 = T-Cobbler

nets:
  N1: U1.VCC, T-Cobbler1.5V0#21
  N2: U1.GND, T-Cobbler1.GND#22
  N3: U1.SCK, T-Cobbler1.SCL1
  N4: U1.SDI, T-Cobbler1.SDA1

custom parts:
  BMP280 Module: The BMP280 is an absolute barometric pressure sensor especially designed for mobile applications. The sensor module is housed in an extremely compact 8-pin metal-lid LGA package with a footprint of only 2.0 × 2.5 mm2 and 0.95 mm package height. Its small dimensions and its low power consumption of 2.7 µA @1Hz allow the implementation in battery driven devices such as mobile phones, GPS modules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
  T-Cobbler: T-Cobbler for RPi B+ and Rpi2 from SunFounder
