# Fritzing sketch 32_MPU6050 (saved by Fritzing 0.9.2b)
breadboards: 1

parts:
  T-Cobbler1 = T-Cobbler
  module1 = MPU6050

nets:
  N1: T-Cobbler1.SDA1, module1.SDA
  N2: T-Cobbler1.SCL1, module1.SCL
  N3: T-Cobbler1.5V0#20, module1.VCC
  N4: T-Cobbler1.GND#22, module1.GND

notes:
  MPU6050

custom parts:
  T-Cobbler: T-Cobbler for RPi B+ and Rpi2 from SunFounder
  MPU6050: MPU6050 Gyro Acceleration module of SunFounder Sensor Kit
