# Fritzing sketch 33_DS1302 (saved by Fritzing 0.9.3b)
breadboards: 1

parts:
  T-Cobbler1 = T-Cobbler
  module7 = DS1302 RTC

nets:
  N1: T-Cobbler1.3V3#0, module7.VCC
  N2: T-Cobbler1.GND#4, module7.GND
  N3: T-Cobbler1.GPIO23, module7.SCL
  N4: T-Cobbler1.GPIO24, module7.SDA
  N5: T-Cobbler1.GPIO25, module7.RST

notes:
  DS1302

custom parts:
  T-Cobbler: T-Cobbler for RPi B+ and Rpi2 from SunFounder
  DS1302 RTC: DS1302RTC module of SunFounder Sensor Kit
