# Fritzing sketch 33_DS1302_C (saved by Fritzing 0.9.2b)
breadboards: 1

parts:
  T-Cobbler1 = T-Cobbler
  module7 = DS1302 RTC

nets:
  N1: T-Cobbler1.GPIO17, module7.SCL
  N2: T-Cobbler1.GPIO27, module7.RST
  N3: T-Cobbler1.5V0#20, module7.VCC
  N4: T-Cobbler1.GND#22, module7.GND
  N5: T-Cobbler1.GPIO18, module7.SDA

notes:
  DS1302

custom parts:
  T-Cobbler: T-Cobbler for RPi B+ and Rpi2 from SunFounder
  DS1302 RTC: DS1302RTC module of SunFounder Sensor Kit
