# Fritzing sketch 34_Tracking (saved by Fritzing 0.9.2b)
breadboards: 1

parts:
  T-Cobbler1 = T-Cobbler
  module8 = Tracking

nets:
  N1: T-Cobbler1.GPIO17, module8.SIG
  N2: T-Cobbler1.5V0#20, module8.VCC
  N3: T-Cobbler1.GND#22, module8.GND

notes:
  Tracking

custom parts:
  T-Cobbler: T-Cobbler for RPi B+ and Rpi2 from SunFounder
  Tracking: Tracking module of SunFounder Sensor Kit
