# Fritzing sketch 35_Expand02 (saved by Fritzing 0.9.3b)
breadboards: 1

parts:
  T-Cobbler1 = T-Cobbler
  module10 = PCF8591
  module14 = RGB LED
  module15 = DS18B20 module
  module16 = Buzzer
  module17 = JoyStick

nets:
  VCC: T-Cobbler1.3V3#0, module10.VCC, module14.VCC, module15.VCC, module16.VCC, module17.VCC
  N1: T-Cobbler1.SDA1, module10.SDA
  N2: T-Cobbler1.SCL1, module10.SCL
  N3: T-Cobbler1.GPIO4, module15.SIG
  N4: T-Cobbler1.GPIO17, module14.R
  N5: T-Cobbler1.GPIO27, module14.B
  N6: T-Cobbler1.GPIO22, module16.SIG
  GND: T-Cobbler1.GND#22, module10.GND, module15.GND, module16.GND, module17.GND
  N7: T-Cobbler1.GPIO18, module14.G
  N8: module10.AIN1, module17.X
  N9: module10.AIN2, module17.BT
  N10: module10.AIN0, module17.Y

notes:
  PCF8591
  Joystick
  Active Buzz
  RGB LED
  DS18B20

custom parts:
  T-Cobbler: T-Cobbler for RPi B+ and Rpi2 from SunFounder
  PCF8591: PCF8591 ADC module for SunFounder Sensor Kit
  RGB LED: RGB LED module of SunFounder Sensor Kit
  DS18B20 module: DS18B20 module from SunFounder Sensor Kit
  Buzzer: Buzzer module of SunFounder Sensor Kit
  JoyStick: JoyStick module of SunFounder Sensor Kit
